# Fritzing sketch DisplayBank (saved by Fritzing 0.9.2b)
circuit board: 7.03586cm x 3.97962cm
breadboards: 1

parts:
  U1 = 74HC595 [package="DIP16 [THT]"]
  U2 = 74HC595 [package="DIP16 [THT]"]
  U3 = attiny85 [package=dip]
  R1 = Resistor [tolerance=±5% resistance=220 package=THT]
  R2 = Resistor [tolerance=±5% resistance=220 package=THT]
  R3 = Resistor [tolerance=±5% resistance=220 package=THT]
  R4 = Resistor [tolerance=±5% resistance=220 package=THT]
  R5 = Resistor [tolerance=±5% resistance=10k package=THT]
  LED1 = 7-SEGMENT-4DIGIT-YOUNGSUN [package=7-segment-4digit-youngsun-longpads]
  JP1 = Header 6 [package=molex-1x6-ra]

nets:
  N1: U1.Q1, LED1.B
  N2: U1.Q2, LED1.C
  N3: U1.Q3, LED1.D
  N4: U1.Q4, LED1.E
  N5: U1.Q5, LED1.F
  N6: U1.Q6, LED1.G
  N7: U1.Q7, LED1.DP
  GND: U1.GND, U1.OE, U2.GND, U2.OE, U3.Pin_4, JP1.1
  N8: U1.Q7', U2.DS
  VCC: U1.MR, U1.VCC, U2.MR, U2.VCC, U3.Pin_8, R5.Pin_1, JP1.3
  N9: U1.SH_CP, U2.SH_CP, U3.Pin_5, JP1.6
  N10: U1.ST_CP, U2.ST_CP, U3.Pin_3
  N11: U1.DS, U3.Pin_2
  N12: U1.Q0, LED1.A
  N13: U2.Q1, LED1.COL-C
  N14: U2.Q2, LED1.APOS-A
  N15: U2.Q3, LED1.APOS-C
  N16: U2.Q4, R4.Pin_1
  N17: U2.Q5, R3.Pin_1
  N18: U2.Q6, R2.Pin_1
  N19: U2.Q7, R1.Pin_1
  N20: U2.Q0, LED1.COL-A
  N21: U3.Pin_1, R5.Pin_0, JP1.2
  N22: U3.Pin_6, JP1.5
  N23: U3.Pin_7, JP1.4
  N24: R1.Pin_0, LED1.DIG4
  N25: R2.Pin_0, LED1.DIG3
  N26: R3.Pin_0, LED1.DIG2
  N27: R4.Pin_0, LED1.DIG1
