# Fritzing sketch NaniteSMD (saved by Fritzing 0.9.2b)
circuit board: 3.63753cm x 1.27027cm
breadboards: 1

parts:
  3_6v = DIODE-ZENER [package=diode-zener]
  3_6v_2 = DIODE-ZENER [package=diode-zener]
  USB_MiniB = USB Connectors [package=usb-minib-nostop]
  Tiny85 = ATTINY13 [package=so]
  S1 = Momentary Switch [package=tactile_switch_smd]
  U1 = attiny85 [package=dip]
  1_5k = Resistor [tolerance=±5% resistance=1.5k package="0603 [SMD]"]
  10k = Resistor [tolerance=±5% resistance=10k package="0603 [SMD]"]
  68 = Resistor [tolerance=±0.05% resistance=68 package="0603 [SMD]"]
  68_2 = Resistor [tolerance=±0.05% resistance=68 package="0603 [SMD]"]
  C1 = Ceramic Capacitor [capacitance=100nF package="0603 [SMD, multilayer]"]
  LED1 = smd LED [color="Red (633nm)" package="0603 [SMD]"]

nets:
  N1: 3_6v.C, USB_MiniB.D-, 1_5k.Pin_0, 68.Pin_0
  GND: 3_6v.A, 3_6v_2.A, USB_MiniB.GND, Tiny85.GND, S1.3, U1.Pin_4, C1.0
  N2: 3_6v_2.C, USB_MiniB.D+, 68_2.Pin_0
  5V: USB_MiniB.VBUS, Tiny85.VCC, U1.Pin_8, 1_5k.Pin_1, 10k.Pin_0, C1.1
  N3: Tiny85.PB5(NRES), S1.1, U1.Pin_1, LED1.cathode
  N4: Tiny85.PB3(ADC3), U1.Pin_3, 68.Pin_1
  N5: Tiny85.PB4(ADC2), U1.Pin_2, 68_2.Pin_1
  N6: Tiny85.PB0(MOSI), U1.Pin_5
  N7: Tiny85.PB1(MISO), U1.Pin_6
  N8: Tiny85.PB2(SCK_ADC1), U1.Pin_7
  N9: 10k.Pin_1, LED1.anode

notes:
  WhileyLabs
