# Fritzing sketch Games Console (saved by Fritzing 0.8.7b)
circuit board: 8.46667cm x 5.64444cm
breadboards: 1

parts:
  U1 = Thumb Joystick [package=joystick]
  U2 = attiny85 [package=dip]
  Power_plug1 = Power plug

nets:
  N1: U1.V+, U1.H+, U2.Pin_8, Power_plug1.VCC
  N2: U1.V, U2.Pin_2
  N3: U1.H, U2.Pin_6
  N4: U1.H-, U1.V-, U2.Pin_4, Power_plug1.GND
